# Fritzing sketch smart-backlight (saved by Fritzing 0.9.4)
circuit board: 4.84007cm x 3.07445cm
breadboards: 1

parts:
  S1 = SWITCH-MOMENTARY-2 [package=tactile-pth-12mm]
  C1 = Electrolytic Capacitor [capacitance=22µF voltage=20V package="200 mil [THT, electrolytic]"]
  J1 = Camdenboss CTB0158-6 [part_number=6 package=THT]
  Q2 = npn-Powertransistor [package="TO220 [THT]"]
  Q1 = npn-Powertransistor [package="TO220 [THT]"]
  U1 = NodeMCU V3.0

nets (from the schematic view):
  N1: S1.1, C1.-, U1.GND#6, U1.GND#13
  N2: S1.2, C1.+, U1.D5
  dev2 -: J1.pin1, Q1.collector
  +12V: J1.pin2, J1.pin4, J1.pin6, U1.Vin
  dev1 -: J1.pin3, Q2.collector
  0V: J1.pin5, Q1.emitter
  N3: Q2.base, U1.D1
  N4: Q2.emitter, U1.GND#41
  N5: Q1.base, U1.D2

custom parts:
  NodeMCU V3.0: ESP8266 based NodeMCU
